# Fritzing sketch Balanza (saved by Fritzing 0.9.3b)
breadboards: 1

parts:
  Componente1 = Arduino Nano (Rev3.0)  # not connected
  Componente2 = HX711 Weighing Sensor Module
  Load_Cell1 = Load Cell - Red/white/black/green

nets:
  N1: Componente2.E+, Load_Cell1.wire1
  N2: Componente2.E-, Load_Cell1.wire3
  N3: Componente2.A+, Load_Cell1.wire2
  N4: Componente2.A-, Load_Cell1.wire4

notes:
  B+ B- A+ A- E- E+
  Vcc SCK DT GND

custom parts:
  Load Cell - Red/white/black/green: A rectangle load cell/weighting pressure Sensor with four wires - Red, white, black, green. Normally corresponding with E+, E-, A+, A- respectively.
