# Fritzing sketch Balanza_Bluetooth (saved by Fritzing 0.9.3b)
breadboards: 1

parts:
  Componente1 = Arduino Nano (Rev3.0)
  Componente2 = HX711 Weighing Sensor Module
  Load_Cell1 = Load Cell - Red/white/black/green
  Componente3 = Bluetooth HC-05 Gomcu

nets:
  GND: Componente1.GND, Componente3.GND
  N1: Componente1.D9, Componente3.KEY
  N2: Componente1.D10, Componente3.TXD
  N3: Componente1.D11/MOSI, Componente3.RXD
  5V: Componente1.5V, Componente3.Vcc
  N4: Componente2.E+, Load_Cell1.wire1
  N5: Componente2.E-, Load_Cell1.wire3
  N6: Componente2.A+, Load_Cell1.wire2
  N7: Componente2.A-, Load_Cell1.wire4

notes:
  B+ B- A+ A- E- E+
  Vcc SCK DT GND

custom parts:
  Load Cell - Red/white/black/green: A rectangle load cell/weighting pressure Sensor with four wires - Red, white, black, green. Normally corresponding with E+, E-, A+, A- respectively.
  Bluetooth HC-05 Gomcu: Modulo HC05 Bluetooth con los pines GOMCU
