# Fritzing sketch Balanza_HX711_ESP32 (saved by Fritzing 0.9.3b)
breadboards: 1

parts:
  Componente2 = HX711 Weighing Sensor Module
  Load_Cell1 = Load Cell - Red/white/black/green
  MH-ET_LIVE_ESP32_DEVKIT1 = MH-ET LIVE ESP32 DEVKIT 38 pins  # not connected

nets:
  N1: Componente2.E+, Load_Cell1.wire1
  N2: Componente2.E-, Load_Cell1.wire3
  N3: Componente2.A+, Load_Cell1.wire2
  N4: Componente2.A-, Load_Cell1.wire4

notes:
  B+ B- A+ A- E- E+
  Vcc SCK DT GND
  GPIO18 GPIO19

custom parts:
  Load Cell - Red/white/black/green: A rectangle load cell/weighting pressure Sensor with four wires - Red, white, black, green. Normally corresponding with E+, E-, A+, A- respectively.
  MH-ET LIVE ESP32 DEVKIT 38 pins: http://mh.nodebb.com/topic/2/mh-et-live-esp32-devkit
