# Fritzing sketch Config_Serial (saved by Fritzing 1.0.5)
breadboards: 1

parts:
  Componente1 = Arduino Uno (Rev3)
  R1 = Resistor [tolerance=±5% power=0.25 resistance=220 package=THT]
  S1 = Pushbutton [package="[THT]"]
  R2 = Resistor [tolerance=±5% power=0.25W resistance=10k package=THT]
  LED1 = RGB LED (com. cathode, rgb) [color="Red (633nm)" current=0.030A package="5 mm [THT]"]

nets:
  N1: Componente1.D9_PWM, LED1.blue_anode
  N2: Componente1.D10_PWM/SS, LED1.green_anode
  N3: Componente1.D11_PWM/MOSI, LED1.red_anode
  N4: Componente1.GND, R1.Pin_0, R2.Pin_0
  N5: Componente1.D2, S1.Pin_1, S1.Pin_2, R2.Pin_1
  N6: Componente1.5V, S1.Pin_3, S1.Pin_4
  N7: R1.Pin_1, LED1.common_cathode
