# Fritzing sketch ServESP32 (saved by Fritzing 0.9.10b)
breadboards: 1

parts:
  MH-ET_LIVE_ESP32_DEVKIT1 = MH-ET LIVE ESP32 DEVKIT 38 pins
  R1 = Resistor [tolerance=±5% power=0.25 resistance=1k package=THT]
  R2 = Rotary Potentiometer (Small) [maximum_resistance=10kΩ knob_status=50% power=0.5W package=THT]
  S1 = Pushbutton [package="[THT]"]
  R3 = Resistor [tolerance=±5% power=0.25 resistance=100 package=THT]
  M1 = RioRand LM2596
  VCC2 = Battery block 9V

nets:
  N1: MH-ET_LIVE_ESP32_DEVKIT1.3V3, R1.Pin_1, S1.Pin_1, S1.Pin_2, M1.Pin_3
  N2: MH-ET_LIVE_ESP32_DEVKIT1.IO34, R2.wiper
  N3: MH-ET_LIVE_ESP32_DEVKIT1.IO13, S1.Pin_3, S1.Pin_4, R3.Pin_1
  N4: MH-ET_LIVE_ESP32_DEVKIT1.GND, R2.leg2, R3.Pin_0, M1.Pin_4
  N5: R1.Pin_0, R2.leg1
  N6: M1.Pin_1, VCC2.+
  N7: M1.Pin_2, VCC2.-

notes:
  [escriba Ajustar a 3.3V]

custom parts:
  MH-ET LIVE ESP32 DEVKIT 38 pins: http://mh.nodebb.com/topic/2/mh-et-live-esp32-devkit
