# Fritzing sketch HC05_Bluetooth (saved by Fritzing 0.9.9b)

parts:
  Parte2 = Arduino Uno (Rev3)
  HC-05 = Bluetooth HC-05 Macho

nets:
  N1: Parte2.D8, HC-05.VCC
  N2: Parte2.D9_PWM, HC-05.Key
  N3: Parte2.D10_PWM/SS, HC-05.TXD
  N4: Parte2.D11_PWM/MOSI, HC-05.RXD
  GND: Parte2.GND, HC-05.GND

notes:
  RX y TX indican donde conectarlo, estan invertidos con respecto a los pines.

// code stored in the sketch: E5_Bluetooch.ino
/*  ----------------------------------------------------------------
Fco. Javier Rodriguez Navarro   www.pinguytaz.net

  
Ejemplo para probar la configuración de Bluetooch.
Tanto la programación mediante comandos AT y la consola y despues el 
control desde Bluetooch.

Las acciones por Bluetooch son:
    Si se pulsa el boton, envia el valor del potenciometro al movil.
    Si desde movil se envia

DATOS ALMACENAMIENTO:  XXXXXX bytes. (Programa) YYYYY (Variables)
      Programa XXX  bytes (16%)
      V. Globales YYY bytes (13%)
--------------------------------------------------------------------  
*/
// Usaremos la libreria „SoftwareSerial“ para usar otros pines de comunicacion
// y dejar libre la consola serie. Que usa el USB y comunica por el 1 y 0.
#include <SoftwareSerial.h> // Comunicación serie en otros pins
 
// Creamos la clase
SoftwareSerial BT(10,11); //10 RX, 11 TX.

// Definicion de pines
const int Pvcc = 8; // Alimentación, para poder apagarlo.
const int Pkey = 9; // Se pone a nivel alto para comandos,
const int PA0 = A0; // Lectura del potenciometro
const int Ppulsa = 2; // Pulsador.
const int Pled = 7;  // Led rosa
const int Projo = 3; // Pata roja del RGB
const int Pverde = 5; // Pata verde del RGB
const int Pazul = 6; // Pata azul del RGB

int parpadeo = 3;
unsigned long tparpadeo;  // OJO es el tiempo en millis para evitar desbordamiento.
boolean eparpadeo = HIGH;

void setup() 
{
  String respuesta="";
  
  BT.begin(9600); //Velocidad del puerto del módulo Bluetooth
  Serial.begin(9600); // Velocidad consola.
  BT.begin(38400);  // Velocidad del equipo HC-05
  
  // Definición de Pines
  pinMode(Pvcc, OUTPUT); // Alimentación y preparar Reset,
  pinMode(Pkey, OUTPUT); // Al poner en HIGH forzaremos el modo AT
  pinMode(Ppulsa, INPUT);  // Boton para lectura.
  pinMode(Pled, OUTPUT);   // Led que parpadea
  pinMode(Projo, OUTPUT); 
  pinMode(Pverde, OUTPUT); 
  pinMode(Pazul, OUTPUT); 
  

  modo_Comando(HIGH); // Activamos modo comando.
  delay(1000); 

  // Una primera configuración.
  // Serial.println(Comando("AT+ORGL"));   // Reinicia a sus datos originales.
  //Serial.println(comando("AT+VERSION?")); // Da la version
  //Serial.println(comando("AT+UART?"));  // Configuración de velocidad
  //Serial.println(comando("AT+NAME=HC-EJ5")); // Nombre
  Serial.println(comando("AT+NAME?")); // Nombre
  Serial.println(comando("AT+PSWD?")); // Clave de acceso
  //Serial.println(comando("AT+ROLE=0")); // Modo 0-Esclavo, 1-maestro y 2 Loop
  
  modo_Comando(LOW); // Activamos modo comunicacion
  delay(500); 
}

void loop() 
{
  String respuesta="";
  char dato;

  int cuenta, lectura, valor;
  String cadena;
  int rojo,verde,azul,coma1, coma2;
  

//  Controla el pulsador para enviar los datos que envie el potenciometro.
 if (digitalRead(Ppulsa) == HIGH)
 {
    while (digitalRead(Ppulsa)) ; // Evitamos que se envien varios datos con una pulsación.
    lectura = analogRead(PA0); // Leemos el valor de la entrada analogica A0
    valor = map(lectura,0,1023,100,1000);  // Lo escalamos entre 0-255
    escribe("Leido: " + String(lectura));
    escribe("Escalado: "+ String(valor));
 }

 // Control del parpadeo cada vez que pase por el bucle miramos si lo enciende o apaga.
 if (parpadeo != 0 && tparpadeo < millis()) // Si es 0 se supone que es siempre apagado.
 {
    tparpadeo = millis() + parpadeo*1000;
    eparpadeo = !eparpadeo;
    digitalWrite(Pled,eparpadeo);
 }
 

 //  Controla si le llega un comando
 cadena = lee();
 if (cadena != "") // Si llego algo se analiza a ver que comando es
 {
    Serial.println("Llego: "+cadena);
    switch (cadena[0])
    { 
        case 'C':
           coma1 = cadena.indexOf(',');
           coma2 = cadena.indexOf(',', coma1+1);
           rojo = cadena.substring(2,coma1).toInt();
           if (rojo > 255) rojo = 255;
           verde = cadena.substring(coma1+1, coma2).toInt();
           if (verde > 255) verde = 255;
           azul = cadena.substring(coma2+1).toInt();
           if (azul > 255) azul = 255;
           analogWrite(Projo,rojo);
           analogWrite(Pverde,verde);
           analogWrite(Pazul,azul);
           break;
        case 'L':
           digitalWrite(Pled,LOW);
           // Recogemos el tiempo;
           parpadeo = cadena.substring(2).toInt();
           if (parpadeo != 0)
           {          
              eparpadeo = HIGH;
              digitalWrite(Pled,eparpadeo);
              tparpadeo = millis() + parpadeo*1000;
            }
           break;
        default: 
           Serial.println("ERROR de comando");
           break;
    }
  
 }


//  Para consola y poder depurar
  cuenta = BT.available();
  if (cuenta > 0)
  {
    Serial.write(BT.read());
    cuenta =0;
  }

  cuenta = Serial.available();
  if (cuenta > 0)
  {
    dato = Serial.read();
    BT.write(dato);
    cuenta = 0;
  }
///   Fin tramo de consola
}

//////////////////////////////////////////////////////
//   Modo_Comando(HIGH-Comamdo, LOW-Transmisión)
//     
//   Reinicia el modulo en modo comando o transmisión
/////////////////////////////////////////////////////
void modo_Comando(boolean modo)
{
  digitalWrite(Pvcc, LOW); // Apaga el modulo
  delay (500) ;
  digitalWrite(Pkey, modo);  // Pone el modo
  delay (500) ;
  digitalWrite(Pvcc, HIGH); // Enciendo el modulo en el estado.

  if (modo) Serial.println("Activamos el modo comando del HC-05");
  else Serial.println("Activamos el modo transmisión");
}
  
/////////////////////////////////////////////////////////
//   Comando(String comando)
//
//       Envia un comando al dispositivos, acordarse de poner en modo comando.
/////////////////////////////////////////////////////////
String comando(String at)
{
  String resultado = "";
      
  // Vacia Buffer del dispositivo
  while (BT.available() > 0) Serial.write(BT.read());

  escribe(at);
 
  delay(1000);  // Esperamos un segundo ya que no se puede enviar antes otro.

  resultado = lee();
  return resultado;
}


//////////////////////////////////////////////////////
//   Escribe(String cadena)
//     
//   Envia al dispositivo una cadena
/////////////////////////////////////////////////////
void escribe(String cadena)
{
   char c;
   
   for (int i=0; i < cadena.length(); i++) 
   {
       c = cadena[i];
       BT.write(c);
    }

  // Enviamos el CR+lf necesario para finalizar el comando
  BT.write('\r');  
  BT.write('\n');
}

//////////////////////////////////////////////////////
//   String lee()
//     
//   Recibe datos.
/////////////////////////////////////////////////////
String lee()
{
  String resultado="";
  char c;
  
  while(BT.available() > 0)
  {
       c = BT.read();
       resultado = resultado + c;    
  }
  return resultado;
}

// code stored in the sketch: E5_Bluetooth.ino
/*  ----------------------------------------------------------------
Fco. Javier Rodriguez Navarro   www.pinguytaz.net

  
Ejemplo para probar la configuración de Bluetooch.
Tanto la programación mediante comandos AT y la consola y despues el 
control desde Bluetooch.

Las acciones por Bluetooch son:
    Si se pulsa el boton, envia el valor del potenciometro al movil.
    Si desde movil se envia "L <x>" parpadea el led rosa cada x segundos
    Si desde el movil se envia "C <r>,<g>,>b>" pone esos valore en el led RGB

DATOS ALMACENAMIENTO: 
      Programa 8.880 bytes (27%)
      V. Globales 466 bytes (22%)
--------------------------------------------------------------------  
*/
// Usaremos la libreria „SoftwareSerial“ para usar otros pines de comunicacion
// y dejar libre la consola serie. Que usa el USB y comunica por el 1 y 0.
#include <SoftwareSerial.h> // Comunicación serie en otros pins
 
// Creamos la clase
SoftwareSerial BT(10,11); //10 RX, 11 TX.

// Definicion de pines
const int Pvcc = 8; // Alimentación, para poder apagarlo.
const int Pkey = 9; // Se pone a nivel alto para comandos,
const int PA0 = A0; // Lectura del potenciometro
const int Ppulsa = 2; // Pulsador.
const int Pled = 7;  // Led rosa
const int Projo = 3; // Pata roja del RGB
const int Pverde = 5; // Pata verde del RGB
const int Pazul = 6; // Pata azul del RGB

int parpadeo = 3;
unsigned long tparpadeo;  // OJO es el tiempo en millis para evitar desbordamiento.
boolean eparpadeo = HIGH;

void setup() 
{
  String respuesta="";
  
  BT.begin(9600); //Velocidad del puerto del módulo Bluetooth
  Serial.begin(9600); // Velocidad consola.
  BT.begin(38400);  // Velocidad del equipo HC-05
  
  // Definición de Pines
  pinMode(Pvcc, OUTPUT); // Alimentación y preparar Reset,
  pinMode(Pkey, OUTPUT); // Al poner en HIGH forzaremos el modo AT
  pinMode(Ppulsa, INPUT);  // Boton para lectura.
  pinMode(Pled, OUTPUT);   // Led que parpadea
  pinMode(Projo, OUTPUT); 
  pinMode(Pverde, OUTPUT); 
  pinMode(Pazul, OUTPUT); 
  

  modo_Comando(HIGH); // Activamos modo comando.
  delay(1000); 

  // Una primera configuración.
  // Serial.println(Comando("AT+ORGL"));   // Reinicia a sus datos originales.
  //Serial.println(comando("AT+VERSION?")); // Da la version
  //Serial.println(comando("AT+UART?"));  // Configuración de velocidad
  //Serial.println(comando("AT+NAME=HC-EJ5")); // Nombre
  Serial.println(comando("AT+NAME?")); // Nombre
  Serial.println(comando("AT+PSWD?")); // Clave de acceso
  //Serial.println(comando("AT+ROLE=0")); // Modo 0-Esclavo, 1-maestro y 2 Loop
  
  modo_Comando(LOW); // Activamos modo comunicacion
  delay(500); 
}

void loop() 
{
  String respuesta="";
  char dato;

  int cuenta, lectura, valor;
  String cadena;
  int rojo,verde,azul,coma1, coma2;
  

//  Controla el pulsador para enviar los datos que envie el potenciometro.
 if (digitalRead(Ppulsa) == HIGH)
 {
    while (digitalRead(Ppulsa)) ; // Evitamos que se envien varios datos con una pulsación.
    lectura = analogRead(PA0); // Leemos el valor de la entrada analogica A0
    valor = map(lectura,0,1023,100,1000);  // Lo escalamos entre 0-255
    escribe("Leido: " + String(lectura));
    escribe("Escalado: "+ String(valor));
 }

 // Control del parpadeo cada vez que pase por el bucle miramos si lo enciende o apaga.
 if (parpadeo != 0 && tparpadeo < millis()) // Si es 0 se supone que es siempre apagado.
 {
    tparpadeo = millis() + parpadeo*1000;
    eparpadeo = !eparpadeo;
    digitalWrite(Pled,eparpadeo);
 }
 

 //  Controla si le llega un comando
 cadena = lee();
 if (cadena != "") // Si llego algo se analiza a ver que comando es
 {
    Serial.println("Llego: "+cadena);
    switch (cadena[0])
    { 
        case 'C':
           coma1 = cadena.indexOf(',');
           coma2 = cadena.indexOf(',', coma1+1);
           rojo = cadena.substring(2,coma1).toInt();
           if (rojo > 255) rojo = 255;
           verde = cadena.substring(coma1+1, coma2).toInt();
           if (verde > 255) verde = 255;
           azul = cadena.substring(coma2+1).toInt();
           if (azul > 255) azul = 255;
           analogWrite(Projo,rojo);
           analogWrite(Pverde,verde);
           analogWrite(Pazul,azul);
           break;
        case 'L':
           digitalWrite(Pled,LOW);
           // Recogemos el tiempo;
           parpadeo = cadena.substring(2).toInt();
           if (parpadeo != 0)
           {          
              eparpadeo = HIGH;
              digitalWrite(Pled,eparpadeo);
              tparpadeo = millis() + parpadeo*1000;
            }
           break;
        default: 
           Serial.println("ERROR de comando");
           break;
    }
 }
}

//////////////////////////////////////////////////////
//   Modo_Comando(HIGH-Comamdo, LOW-Transmisión)
//     
//   Reinicia el modulo en modo comando o transmisión
/////////////////////////////////////////////////////
void modo_Comando(boolean modo)
{
  digitalWrite(Pvcc, LOW); // Apaga el modulo
  delay (500) ;
  digitalWrite(Pkey, modo);  // Pone el modo
  delay (500) ;
  digitalWrite(Pvcc, HIGH); // Enciendo el modulo en el estado.

  if (modo) Serial.println("Activamos el modo comando del HC-05");
  else Serial.println("Activamos el modo transmisión");
}
  
/////////////////////////////////////////////////////////
//   Comando(String comando)
//
//       Envia un comando al dispositivos, acordarse de poner en modo comando.
/////////////////////////////////////////////////////////
String comando(String at)
{
  String resultado = "";
      
  // Vacia Buffer del dispositivo
  while (BT.available() > 0) Serial.write(BT.read());

  escribe(at);
 
  delay(1000);  // Esperamos un segundo ya que no se puede enviar antes otro.

  resultado = lee();
  return resultado;
}


//////////////////////////////////////////////////////
//   Escribe(String cadena)
//     
//   Envia al dispositivo una cadena
/////////////////////////////////////////////////////
void escribe(String cadena)
{
   char c;
   
   for (int i=0; i < cadena.length(); i++) 
   {
       c = cadena[i];
       BT.write(c);
    }

  // Enviamos el CR+lf necesario para finalizar el comando
  BT.write('\r');  
  BT.write('\n');
}

//////////////////////////////////////////////////////
//   String lee()
//     
//   Recibe datos.
/////////////////////////////////////////////////////
String lee()
{
  String resultado="";
  char c;
  
  while(BT.available() > 0)
  {
       c = BT.read();
       resultado = resultado + c;    
  }
  return resultado;
}
