# Fritzing sketch Ej_I2C (saved by Fritzing 0.9.9b)
breadboards: 2

parts:
  MH-ET_LIVE_ESP32_DEVKIT1 = MH-ET LIVE ESP32 DEVKIT 38 pins
  R1 = Resistor [tolerance=±5% power=0.25 resistance=4.7k package=THT]
  Componente1 = Arduino Nano (Rev3.0)
  S2 = Pushbutton [package="[THT]"]
  R7 = Resistor [tolerance=±5% resistance=10k power=0.25 package=THT]
  R8 = Resistor [tolerance=±5% power=0.25 resistance=4.7k package=THT]
  R9 = Rotary Potentiometer (Small) [maximum_resistance=100kΩ package=THT]
  TFT1 = 1.44" SPI TFT Graphics Display 128x128 [package=THT]
  R10 = Resistor [tolerance=±5% power=0.25 resistance=470 package=THT]
  LED1 = LED - 5mm [color="Red (633nm)" current=0.030 package="5 mm [THT]"]

nets:
  N1: MH-ET_LIVE_ESP32_DEVKIT1.3V3, R9.leg2
  N2: MH-ET_LIVE_ESP32_DEVKIT1.IO34, R9.wiper
  N3: MH-ET_LIVE_ESP32_DEVKIT1.IO25, R10.Pin_1
  N4: MH-ET_LIVE_ESP32_DEVKIT1.GND, R9.leg1, LED1.cathode
  N5: MH-ET_LIVE_ESP32_DEVKIT1.IO22, R8.Pin_1
  N6: MH-ET_LIVE_ESP32_DEVKIT1.IO21, R1.Pin_1
  N7: R1.Pin_0, Componente1.5V, S2.Pin_3, S2.Pin_4, R8.Pin_0, TFT1.pin2
  N8: Componente1.D8, TFT1.pin6
  N9: Componente1.D9, TFT1.pin5
  N10: Componente1.D10, TFT1.pin7
  N11: Componente1.D11/MOSI, TFT1.pin4
  N12: Componente1.D12/MISO, S2.Pin_1, S2.Pin_2, R7.Pin_0
  N13: Componente1.GND, R7.Pin_1, TFT1.pin1
  N14: Componente1.D13/SCK, TFT1.pin3
  N15: R10.Pin_0, LED1.anode

notes:
  Rx
  CS
  GND
  Comportamiento I2C Maestro
  SDA
  SCL
  Comportamiento I2C Esclavo
  DC
  RST
  BLK
  VDD

custom parts:
  MH-ET LIVE ESP32 DEVKIT 38 pins: http://mh.nodebb.com/topic/2/mh-et-live-esp32-devkit
  1.44" SPI TFT Graphics Display 128x128: This is for https://www.amazon.com/gp/product/B07B4BDWCL/ref=ask_ql_qh_dp_hza display. Note that this display is sold with a misprinted silkscreen indicating I2C connections on P2 connector, it is actualy SPI. The P1 connections are non functional on this board from the linked URL seller on Amazon.
