# Fritzing sketch Ej_Serie (saved by Fritzing 0.9.9b)
breadboards: 1

parts:
  Componente1 = Arduino Uno (Rev3)
  MH-ET_LIVE_ESP32_DEVKIT1 = MH-ET LIVE ESP32 DEVKIT 38 pins
  LED1 = RGB LED (com. cathode, rgb) [package="5 mm [THT]"]
  R1 = Resistor [tolerance=±5% power=0.25 resistance=330 package=THT]

nets:
  N1: Componente1.D9_PWM, LED1.blue_anode
  N2: Componente1.D10_PWM/SS, LED1.green_anode
  N3: Componente1.D11_PWM/MOSI, LED1.red_anode
  N4: Componente1.GND, R1.Pin_1
  N5: Componente1.D2, MH-ET_LIVE_ESP32_DEVKIT1.IO17
  N6: Componente1.D3_PWM, MH-ET_LIVE_ESP32_DEVKIT1.IO16
  N7: LED1.common_cathode, R1.Pin_0

notes:
  Pulsador Touch
  Rx
  Tx

custom parts:
  MH-ET LIVE ESP32 DEVKIT 38 pins: http://mh.nodebb.com/topic/2/mh-et-live-esp32-devkit
