# Fritzing sketch ServWEB (saved by Fritzing 0.9.10b)
breadboards: 1

parts:
  MH-ET_LIVE_ESP32_DEVKIT1 = MH-ET LIVE ESP32 DEVKIT 38 pins
  R1 = Resistor [tolerance=±5% power=0.25 resistance=1k package=THT]
  R2 = Rotary Potentiometer (Small) [maximum_resistance=10kΩ knob_status=50% power=0.5W package=THT]
  R3 = Resistor [tolerance=±5% power=0.25 resistance=100 package=THT]
  LED1 = LED - 5mm [color="Red (633nm)" current=0.030 package="5 mm [THT]"]

nets:
  N1: MH-ET_LIVE_ESP32_DEVKIT1.3V3, R1.Pin_1
  N2: MH-ET_LIVE_ESP32_DEVKIT1.IO34, R2.wiper
  N3: MH-ET_LIVE_ESP32_DEVKIT1.IO13, LED1.anode
  N4: MH-ET_LIVE_ESP32_DEVKIT1.GND, R2.leg2, R3.Pin_0
  N5: R1.Pin_0, R2.leg1
  N6: R3.Pin_1, LED1.cathode

custom parts:
  MH-ET LIVE ESP32 DEVKIT 38 pins: http://mh.nodebb.com/topic/2/mh-et-live-esp32-devkit
