# Fritzing sketch E2_ESDigitales (saved by Fritzing 0.9.2b)
circuit board: 8.46667cm x 5.64444cm
breadboards: 1

parts:
  Parte1 = Arduino Uno (Rev3)
  R1 = Resistor [tolerance=±5% resistance=470 package=THT]
  LED1 = LED - 5mm [color="Red (633nm)" package="5 mm [THT]"]
  S1 = Pushbutton [package="[THT]"]
  R2 = Resistor [tolerance=±5% resistance=470 package=THT]
  LED2 = LED - 5mm [color="Blue (430nm)" package="5 mm [THT]"]
  R3 = Resistor [tolerance=±5% resistance=470 package=THT]
  LED3 = LED - 5mm [color="Orange (605nm)" package="5 mm [THT]"]
  R4 = Resistor [tolerance=±5% resistance=470 package=THT]
  LED4 = LED - 5mm [color="Green (555nm)" package="5 mm [THT]"]
  R5 = Resistor [tolerance=±5% resistance=470 package=THT]
  LED5 = LED - 5mm [color="Yellow (574nm)" package="5 mm [THT]"]
  R6 = Resistor [tolerance=±5% resistance=10k package=THT]

nets:
  N1: Parte1.D8, R3.Pin_1
  N2: Parte1.D10_PWM/SS, R2.Pin_1
  N3: Parte1.D12/MISO, R1.Pin_1
  N4: Parte1.GND, LED1.cathode, LED2.cathode, LED3.cathode, LED4.cathode, LED5.cathode, R6.Pin_1
  N5: Parte1.D2, S1.Pin_1, S1.Pin_2, R6.Pin_0
  N6: Parte1.D4, R5.Pin_1
  N7: Parte1.D6_PWM, R4.Pin_1
  N8: Parte1.5V, S1.Pin_3, S1.Pin_4
  N9: R1.Pin_0, LED1.anode
  N10: R2.Pin_0, LED2.anode
  N11: R3.Pin_0, LED3.anode
  N12: R4.Pin_0, LED4.anode
  N13: R5.Pin_0, LED5.anode

// code stored in the sketch: E2_Digitales.ino
/*  ----------------------------------------------------------------
Fco. Javier Rodriguez Navarro   www.pinguytaz.net

  
Probamos entradas digitales y salidas, con variables y bucles
y la consola serie que permite depurar entre otras cosas.


DATOS ALMACENAMIENTO:  32.256 bytes. (Programa) 2.048 (Variables)
      Programa 3.132  (9%)
      V. Globales 288 bytes  (14%)
--------------------------------------------------------------------  
*/

int pulsador = 2; // pin 2 asignado al pulsado
int ledAmarillo = 4; // pin 4 asignado para el LED amarillo
int ledVerde = 6; // pin 4 asignado para el LED verde
int ledNaranja = 8; // pin 6 asignado para el LED naranja
int ledAzul = 10; // pin 8 asignado para el LED azul
int ledRojo = 12; // pin 10 asignado para el LED rojo
int luce=0; // 0 ninguno,1 rojo,2 azul,3 naranja,4 verde,5 azul

void setup() 
{
  Serial.begin(9600);    // abre el Puerto serie y lanza los primeros envios
  Serial.println("-----------");  
  Serial.println("---- INICIO -------");  
  Serial.println("-----------");  

  // Definimos Pines
  pinMode(pulsador, INPUT); // declara pulsador como entrada
  pinMode(ledAmarillo, OUTPUT); // declara LED como salida  
  pinMode(ledVerde, OUTPUT); // declara LED como salida  
  pinMode(ledNaranja, OUTPUT); // declara LED como salida  
  pinMode(ledAzul, OUTPUT); // declara LED como salida
  pinMode(ledRojo, OUTPUT); // declara LED como salida 

  
  // Reinicia los LEDs.
  digitalWrite(ledAmarillo, HIGH);
  digitalWrite(ledVerde, HIGH);
  digitalWrite(ledNaranja, HIGH);
  digitalWrite(ledAzul, HIGH);
  digitalWrite(ledRojo, HIGH);
  delay(1000);
  digitalWrite(ledAmarillo, LOW);
  delay(500);
  digitalWrite(ledVerde, LOW);
  delay(500);
  digitalWrite(ledNaranja, LOW);
  delay(500);
  digitalWrite(ledAzul, LOW);
  delay(500);
  digitalWrite(ledRojo, LOW);
  delay(500);

}

void loop() 
{
   int val = 0;
   val =digitalRead(pulsador);

   if (val == HIGH)
   {
       Serial.print("Cambia a ");  
       cambia();
   }

}

/************************************************************
 * Enciendo todos y los apaga poco a poco, luego deja encendido
 * el siguiente.
 ************************************************************/
void cambia()
{
     luce++;
     if (luce > 5) luce = 1;

     // Primero encendemos y apagamos todas
     digitalWrite(ledAmarillo, HIGH);
     digitalWrite(ledVerde, HIGH);
     digitalWrite(ledNaranja, HIGH);
     digitalWrite(ledAzul, HIGH);
     digitalWrite(ledRojo, HIGH);
     delay(1000);
     digitalWrite(ledAmarillo, LOW);
     digitalWrite(ledVerde, LOW);
     digitalWrite(ledNaranja, LOW);
     digitalWrite(ledAzul, LOW);
     digitalWrite(ledRojo, LOW);
     delay(500);

     switch (luce) 
     {
       case 1: 
          digitalWrite(ledAmarillo, HIGH);
          Serial.println("Amarillo"); 
          break;
      case 2: 
          digitalWrite(ledVerde, HIGH);
          Serial.println("Verde"); 
          break;
      case 3: 
          digitalWrite(ledNaranja, HIGH);
          Serial.println("Naranja"); 
          break;
      case 4: 
          digitalWrite(ledAzul, HIGH);
          Serial.println("Azul"); 
          break;
      case 5: 
          digitalWrite(ledRojo, HIGH);
          Serial.println("Rojo"); 
          break;
     }
     
}
