# Fritzing sketch MotorPasoaPaso (saved by Fritzing 0.9.10b)
breadboards: 1

parts:
  S1 = Pushbutton [package="[THT]"]
  R6 = Resistor [tolerance=±5% resistance=10k power=0.25 package=THT]
  Componente1 = Arduino Nano (Rev3.0) (ICSP)
  M1 = Stepper Motor - Bipolar
  L298N1 = L298N DC motor driver
  J1 = Power Jack [package=power_jack_smd]

nets:
  N1: S1.Pin_1, S1.Pin_2, R6.Pin_0, Componente1.D2
  N2: S1.Pin_3, S1.Pin_4, Componente1.5V
  GND: R6.Pin_1, Componente1.GND, L298N1.GND, J1.GND
  N3: Componente1.D8, L298N1.IN1
  N4: Componente1.D9, L298N1.IN2
  N5: Componente1.D10, L298N1.IN3
  N6: Componente1.D11/MOSI, L298N1.IN4
  N7: M1.A, L298N1.OUT2
  N8: M1.C, L298N1.OUT1
  N9: M1.B, L298N1.OUT4
  N10: M1.D, L298N1.OUT3
  N11: L298N1.12V, J1.GNDBREAK
  N12: L298N1.5V#9, L298N1.ENA
  N13: L298N1.5V#10, L298N1.ENB

notes:
  EN1 y EN2

custom parts:
  L298N DC motor driver: 2x DC motor driver with 78M05 positive voltage regulator (7..35 V) L298N: max 46 V, 2 A Set 5 V Enable jumper to enable 5 V regultor (needed for the L298N) and +5 V output at screw terminal or supply external +5 V at screw terminal Set ENA and/or ENB to +5 V to enable motor permanently or supply ENA and/or ENB with PWM signal IN1 and IN2 set rotation directory for motor A (OUT1/OUT2) IN2 and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

// code stored in the sketch: E2_Digitales.ino
/*  ----------------------------------------------------------------
Fco. Javier Rodriguez Navarro   www.pinguytaz.net

  
Probamos entradas digitales y salidas, con variables y bucles
y la consola serie que permite depurar entre otras cosas.


DATOS ALMACENAMIENTO:  32.256 bytes. (Programa) 2.048 (Variables)
      Programa 3.132  (9%)
      V. Globales 288 bytes  (14%)
--------------------------------------------------------------------  
*/

int pulsador = 2; // pin 2 asignado al pulsado
int ledAmarillo = 4; // pin 4 asignado para el LED amarillo
int ledVerde = 6; // pin 4 asignado para el LED verde
int ledNaranja = 8; // pin 6 asignado para el LED naranja
int ledAzul = 10; // pin 8 asignado para el LED azul
int ledRojo = 12; // pin 10 asignado para el LED rojo
int luce=0; // 0 ninguno,1 rojo,2 azul,3 naranja,4 verde,5 azul

void setup() 
{
  Serial.begin(9600);    // abre el Puerto serie y lanza los primeros envios
  Serial.println("-----------");  
  Serial.println("---- INICIO -------");  
  Serial.println("-----------");  

  // Definimos Pines
  pinMode(pulsador, INPUT); // declara pulsador como entrada
  pinMode(ledAmarillo, OUTPUT); // declara LED como salida  
  pinMode(ledVerde, OUTPUT); // declara LED como salida  
  pinMode(ledNaranja, OUTPUT); // declara LED como salida  
  pinMode(ledAzul, OUTPUT); // declara LED como salida
  pinMode(ledRojo, OUTPUT); // declara LED como salida 

  
  // Reinicia los LEDs.
  digitalWrite(ledAmarillo, HIGH);
  digitalWrite(ledVerde, HIGH);
  digitalWrite(ledNaranja, HIGH);
  digitalWrite(ledAzul, HIGH);
  digitalWrite(ledRojo, HIGH);
  delay(1000);
  digitalWrite(ledAmarillo, LOW);
  delay(500);
  digitalWrite(ledVerde, LOW);
  delay(500);
  digitalWrite(ledNaranja, LOW);
  delay(500);
  digitalWrite(ledAzul, LOW);
  delay(500);
  digitalWrite(ledRojo, LOW);
  delay(500);

}

void loop() 
{
   int val = 0;
   val =digitalRead(pulsador);

   if (val == HIGH)
   {
       Serial.print("Cambia a ");  
       cambia();
   }

}

/************************************************************
 * Enciendo todos y los apaga poco a poco, luego deja encendido
 * el siguiente.
 ************************************************************/
void cambia()
{
     luce++;
     if (luce > 5) luce = 1;

     // Primero encendemos y apagamos todas
     digitalWrite(ledAmarillo, HIGH);
     digitalWrite(ledVerde, HIGH);
     digitalWrite(ledNaranja, HIGH);
     digitalWrite(ledAzul, HIGH);
     digitalWrite(ledRojo, HIGH);
     delay(1000);
     digitalWrite(ledAmarillo, LOW);
     digitalWrite(ledVerde, LOW);
     digitalWrite(ledNaranja, LOW);
     digitalWrite(ledAzul, LOW);
     digitalWrite(ledRojo, LOW);
     delay(500);

     switch (luce) 
     {
       case 1: 
          digitalWrite(ledAmarillo, HIGH);
          Serial.println("Amarillo"); 
          break;
      case 2: 
          digitalWrite(ledVerde, HIGH);
          Serial.println("Verde"); 
          break;
      case 3: 
          digitalWrite(ledNaranja, HIGH);
          Serial.println("Naranja"); 
          break;
      case 4: 
          digitalWrite(ledAzul, HIGH);
          Serial.println("Azul"); 
          break;
      case 5: 
          digitalWrite(ledRojo, HIGH);
          Serial.println("Rojo"); 
          break;
     }
     
}
