# Fritzing sketch SensorTMP36 (saved by Fritzing 0.9.3b)
breadboards: 1

parts:
  MH-ET_LIVE_ESP32_DEVKIT1 = MH-ET LIVE ESP32 DEVKIT 38 pins
  T1 = TMP36 Temperature Sensor [package="TO92 [THT]"]

nets:
  N1: MH-ET_LIVE_ESP32_DEVKIT1.IO34, T1.Vout
  N2: MH-ET_LIVE_ESP32_DEVKIT1.5V, T1.+Vs
  GND: MH-ET_LIVE_ESP32_DEVKIT1.GND, T1.GND

notes:
  +
  -

custom parts:
  MH-ET LIVE ESP32 DEVKIT 38 pins: http://mh.nodebb.com/topic/2/mh-et-live-esp32-devkit
