# Fritzing sketch TMP36Display (saved by Fritzing 0.9.3b)
breadboards: 1

parts:
  T1 = TMP36 Temperature Sensor [package="TO92 [THT]"]
  LCD2004-I2C1 = LCD2004-I2C
  Componente1 = Arduino Uno (Rev3)

nets:
  VCC: T1.+Vs, LCD2004-I2C1.VCC, Componente1.5V
  N1: T1.Vout, Componente1.A0
  GND: T1.GND, LCD2004-I2C1.GND, Componente1.GND
  N2: LCD2004-I2C1.SDA, Componente1.A4/SDA
  N3: LCD2004-I2C1.SCL, Componente1.A5/SCL

notes:
  +
  -

custom parts:
  LCD2004-I2C: A standard character display with 4x20 characters. Comes in many colors with LCM2004 IIC attached.
