# Fritzing sketch TMP36DisplayESP32 (saved by Fritzing 0.9.3b)
breadboards: 1

parts:
  T1 = TMP36 Temperature Sensor [package="TO92 [THT]"]
  LCD2004-I2C1 = LCD2004-I2C
  MH-ET_LIVE_ESP32_DEVKIT1 = MH-ET LIVE ESP32 DEVKIT 38 pins

nets:
  VCC: T1.+Vs, LCD2004-I2C1.VCC, MH-ET_LIVE_ESP32_DEVKIT1.5V
  N1: T1.Vout, MH-ET_LIVE_ESP32_DEVKIT1.IO34
  GND: T1.GND, LCD2004-I2C1.GND, MH-ET_LIVE_ESP32_DEVKIT1.GND
  N2: LCD2004-I2C1.SDA, MH-ET_LIVE_ESP32_DEVKIT1.IO21
  N3: LCD2004-I2C1.SCL, MH-ET_LIVE_ESP32_DEVKIT1.IO22

notes:
  +
  -

custom parts:
  LCD2004-I2C: A standard character display with 4x20 characters. Comes in many colors with LCM2004 IIC attached.
  MH-ET LIVE ESP32 DEVKIT 38 pins: http://mh.nodebb.com/topic/2/mh-et-live-esp32-devkit
