# Fritzing sketch MotorPasoaPasoL298N (saved by Fritzing 1.0.3b)

parts:
  M2 = Stepper Motor - Bipolar
  L298N2 = L298N DC motor driver
  MH-ET_LIVE_ESP32_DEVKIT1 = MH-ET LIVE ESP32 DEVKIT 38 pins
  Power_12V = Power plug
  R1 = Resistor [tolerance=±5% resistance=220 package="0805 [SMD]"]
  LED2 = smd LED [color="Red (633nm)" package="1206 [SMD]"]
  R2 = Resistor [tolerance=±5% resistance=10k package="0805 [SMD]"]
  S1 = Pushbutton [package=THT]

nets:
  N1: M2.A, L298N2.OUT1
  N2: M2.C, L298N2.OUT2
  N3: M2.B, L298N2.OUT3
  N4: M2.D, L298N2.OUT4
  12V: L298N2.12V, Power_12V.VCC
  GND: L298N2.GND, MH-ET_LIVE_ESP32_DEVKIT1.GND#64, Power_12V.GND, R1.Pin_1
  N5: L298N2.5V#7, MH-ET_LIVE_ESP32_DEVKIT1.5V, R2.Pin_0
  N6: L298N2.5V#9, L298N2.ENA
  N7: L298N2.5V#10, L298N2.ENB
  N8: L298N2.IN1, MH-ET_LIVE_ESP32_DEVKIT1.IO19
  N9: L298N2.IN2, MH-ET_LIVE_ESP32_DEVKIT1.IO18
  N10: L298N2.IN3, MH-ET_LIVE_ESP32_DEVKIT1.IO17
  N11: L298N2.IN4, MH-ET_LIVE_ESP32_DEVKIT1.IO16
  N12: MH-ET_LIVE_ESP32_DEVKIT1.IO25, R2.Pin_1, S1.leg1
  N13: MH-ET_LIVE_ESP32_DEVKIT1.GND#58, S1.leg0
  N14: MH-ET_LIVE_ESP32_DEVKIT1.IO15, LED2.anode
  N15: R1.Pin_0, LED2.cathode

notes:
  Jumper Regula
  Jumper EN1 e EN2
  A+ Amarillo
  A- Negro
  B+ Naranja
  B- Marron
  Poner Voltaje adecuado al Motor

custom parts:
  L298N DC motor driver: 2x DC motor driver with 78M05 positive voltage regulator (7..35 V) L298N: max 46 V, 2 A Set 5 V Enable jumper to enable 5 V regultor (needed for the L298N) and +5 V output at screw terminal or supply external +5 V at screw terminal Set ENA and/or ENB to +5 V to enable motor permanently or supply ENA and/or ENB with PWM signal IN1 and IN2 set rotation directory for motor A (OUT1/OUT2) IN2 and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
  MH-ET LIVE ESP32 DEVKIT 38 pins: http://mh.nodebb.com/topic/2/mh-et-live-esp32-devkit

// code stored in the sketch: E2_Digitales.ino
/*  ----------------------------------------------------------------
Fco. Javier Rodriguez Navarro   www.pinguytaz.net

  
Probamos entradas digitales y salidas, con variables y bucles
y la consola serie que permite depurar entre otras cosas.


DATOS ALMACENAMIENTO:  32.256 bytes. (Programa) 2.048 (Variables)
      Programa 3.132  (9%)
      V. Globales 288 bytes  (14%)
--------------------------------------------------------------------  
*/

int pulsador = 2; // pin 2 asignado al pulsado
int ledAmarillo = 4; // pin 4 asignado para el LED amarillo
int ledVerde = 6; // pin 4 asignado para el LED verde
int ledNaranja = 8; // pin 6 asignado para el LED naranja
int ledAzul = 10; // pin 8 asignado para el LED azul
int ledRojo = 12; // pin 10 asignado para el LED rojo
int luce=0; // 0 ninguno,1 rojo,2 azul,3 naranja,4 verde,5 azul

void setup() 
{
  Serial.begin(9600);    // abre el Puerto serie y lanza los primeros envios
  Serial.println("-----------");  
  Serial.println("---- INICIO -------");  
  Serial.println("-----------");  

  // Definimos Pines
  pinMode(pulsador, INPUT); // declara pulsador como entrada
  pinMode(ledAmarillo, OUTPUT); // declara LED como salida  
  pinMode(ledVerde, OUTPUT); // declara LED como salida  
  pinMode(ledNaranja, OUTPUT); // declara LED como salida  
  pinMode(ledAzul, OUTPUT); // declara LED como salida
  pinMode(ledRojo, OUTPUT); // declara LED como salida 

  
  // Reinicia los LEDs.
  digitalWrite(ledAmarillo, HIGH);
  digitalWrite(ledVerde, HIGH);
  digitalWrite(ledNaranja, HIGH);
  digitalWrite(ledAzul, HIGH);
  digitalWrite(ledRojo, HIGH);
  delay(1000);
  digitalWrite(ledAmarillo, LOW);
  delay(500);
  digitalWrite(ledVerde, LOW);
  delay(500);
  digitalWrite(ledNaranja, LOW);
  delay(500);
  digitalWrite(ledAzul, LOW);
  delay(500);
  digitalWrite(ledRojo, LOW);
  delay(500);

}

void loop() 
{
   int val = 0;
   val =digitalRead(pulsador);

   if (val == HIGH)
   {
       Serial.print("Cambia a ");  
       cambia();
   }

}

/************************************************************
 * Enciendo todos y los apaga poco a poco, luego deja encendido
 * el siguiente.
 ************************************************************/
void cambia()
{
     luce++;
     if (luce > 5) luce = 1;

     // Primero encendemos y apagamos todas
     digitalWrite(ledAmarillo, HIGH);
     digitalWrite(ledVerde, HIGH);
     digitalWrite(ledNaranja, HIGH);
     digitalWrite(ledAzul, HIGH);
     digitalWrite(ledRojo, HIGH);
     delay(1000);
     digitalWrite(ledAmarillo, LOW);
     digitalWrite(ledVerde, LOW);
     digitalWrite(ledNaranja, LOW);
     digitalWrite(ledAzul, LOW);
     digitalWrite(ledRojo, LOW);
     delay(500);

     switch (luce) 
     {
       case 1: 
          digitalWrite(ledAmarillo, HIGH);
          Serial.println("Amarillo"); 
          break;
      case 2: 
          digitalWrite(ledVerde, HIGH);
          Serial.println("Verde"); 
          break;
      case 3: 
          digitalWrite(ledNaranja, HIGH);
          Serial.println("Naranja"); 
          break;
      case 4: 
          digitalWrite(ledAzul, HIGH);
          Serial.println("Azul"); 
          break;
      case 5: 
          digitalWrite(ledRojo, HIGH);
          Serial.println("Rojo"); 
          break;
     }
     
}
