# Fritzing sketch MotorPasoaPasoLA4988 (saved by Fritzing 1.0.3b)
breadboards: 1

parts:
  Pololu_A1 = Pololu A4988 [package=SO16]
  M2 = Stepper Motor - Bipolar
  MH-ET_LIVE_ESP32_DEVKIT1 = MH-ET LIVE ESP32 DEVKIT 38 pins
  Power_12V = Power plug
  M3 = RioRand LM2596
  C2 = Capacitor Polarized [package=cpol-radial-100uf-25v]

nets:
  N1: Pololu_A1.RESET, Pololu_A1.SLEEP
  N2: Pololu_A1.STEP, MH-ET_LIVE_ESP32_DEVKIT1.IO14
  N3: Pololu_A1.DIR, MH-ET_LIVE_ESP32_DEVKIT1.IO12
  N4: Pololu_A1.GND#8, M3.Pin_4
  N5: Pololu_A1.VDD, M3.Pin_3
  N6: Pololu_A1.1B, M2.D
  N7: Pololu_A1.1A, M2.B
  N8: Pololu_A1.2A, M2.C
  N9: Pololu_A1.2B, M2.A
  N10: Pololu_A1.GND#14, Power_12V.GND, M3.Pin_2, C2.-
  N11: Pololu_A1.VMOT, Power_12V.VCC, M3.Pin_1, C2.+

notes:
  Ajuste a 5V

custom parts:
  MH-ET LIVE ESP32 DEVKIT 38 pins: http://mh.nodebb.com/topic/2/mh-et-live-esp32-devkit

// code stored in the sketch: E2_Digitales.ino
/*  ----------------------------------------------------------------
Fco. Javier Rodriguez Navarro   www.pinguytaz.net

  
Probamos entradas digitales y salidas, con variables y bucles
y la consola serie que permite depurar entre otras cosas.


DATOS ALMACENAMIENTO:  32.256 bytes. (Programa) 2.048 (Variables)
      Programa 3.132  (9%)
      V. Globales 288 bytes  (14%)
--------------------------------------------------------------------  
*/

int pulsador = 2; // pin 2 asignado al pulsado
int ledAmarillo = 4; // pin 4 asignado para el LED amarillo
int ledVerde = 6; // pin 4 asignado para el LED verde
int ledNaranja = 8; // pin 6 asignado para el LED naranja
int ledAzul = 10; // pin 8 asignado para el LED azul
int ledRojo = 12; // pin 10 asignado para el LED rojo
int luce=0; // 0 ninguno,1 rojo,2 azul,3 naranja,4 verde,5 azul

void setup() 
{
  Serial.begin(9600);    // abre el Puerto serie y lanza los primeros envios
  Serial.println("-----------");  
  Serial.println("---- INICIO -------");  
  Serial.println("-----------");  

  // Definimos Pines
  pinMode(pulsador, INPUT); // declara pulsador como entrada
  pinMode(ledAmarillo, OUTPUT); // declara LED como salida  
  pinMode(ledVerde, OUTPUT); // declara LED como salida  
  pinMode(ledNaranja, OUTPUT); // declara LED como salida  
  pinMode(ledAzul, OUTPUT); // declara LED como salida
  pinMode(ledRojo, OUTPUT); // declara LED como salida 

  
  // Reinicia los LEDs.
  digitalWrite(ledAmarillo, HIGH);
  digitalWrite(ledVerde, HIGH);
  digitalWrite(ledNaranja, HIGH);
  digitalWrite(ledAzul, HIGH);
  digitalWrite(ledRojo, HIGH);
  delay(1000);
  digitalWrite(ledAmarillo, LOW);
  delay(500);
  digitalWrite(ledVerde, LOW);
  delay(500);
  digitalWrite(ledNaranja, LOW);
  delay(500);
  digitalWrite(ledAzul, LOW);
  delay(500);
  digitalWrite(ledRojo, LOW);
  delay(500);

}

void loop() 
{
   int val = 0;
   val =digitalRead(pulsador);

   if (val == HIGH)
   {
       Serial.print("Cambia a ");  
       cambia();
   }

}

/************************************************************
 * Enciendo todos y los apaga poco a poco, luego deja encendido
 * el siguiente.
 ************************************************************/
void cambia()
{
     luce++;
     if (luce > 5) luce = 1;

     // Primero encendemos y apagamos todas
     digitalWrite(ledAmarillo, HIGH);
     digitalWrite(ledVerde, HIGH);
     digitalWrite(ledNaranja, HIGH);
     digitalWrite(ledAzul, HIGH);
     digitalWrite(ledRojo, HIGH);
     delay(1000);
     digitalWrite(ledAmarillo, LOW);
     digitalWrite(ledVerde, LOW);
     digitalWrite(ledNaranja, LOW);
     digitalWrite(ledAzul, LOW);
     digitalWrite(ledRojo, LOW);
     delay(500);

     switch (luce) 
     {
       case 1: 
          digitalWrite(ledAmarillo, HIGH);
          Serial.println("Amarillo"); 
          break;
      case 2: 
          digitalWrite(ledVerde, HIGH);
          Serial.println("Verde"); 
          break;
      case 3: 
          digitalWrite(ledNaranja, HIGH);
          Serial.println("Naranja"); 
          break;
      case 4: 
          digitalWrite(ledAzul, HIGH);
          Serial.println("Azul"); 
          break;
      case 5: 
          digitalWrite(ledRojo, HIGH);
          Serial.println("Rojo"); 
          break;
     }
     
}
