# Fritzing sketch ServoMotor (saved by Fritzing 1.0.2b)
breadboards: 1

parts:
  S1 = Pushbutton [package="[THT]"]
  Componente1 = Arduino Nano (Rev3.0)
  R1 = Resistor [tolerance=±5% power=0.25 resistance=220 package=THT]
  J1 = Basic Servo
  IC1 = Voltage Regulator [package=to-220-alt]
  VCC1 = Battery block 9V
  C1 = Ceramic Capacitor [capacitance=0.1µF voltage=35V package="0603 [SMD, multilayer]"]
  C2 = Ceramic Capacitor [capacitance=0.1µF voltage=35V package="0603 [SMD, multilayer]"]

nets:
  5V: S1.Pin_1, S1.Pin_2, Componente1.5V, J1.vcc, IC1.OUT, C1.1
  N1: S1.Pin_3, S1.Pin_4, Componente1.D2, R1.Pin_1
  GND: Componente1.GND, R1.Pin_0, J1.gnd, IC1.GND, VCC1.-, C1.0, C2.1
  N2: Componente1.D10, J1.pulse
  N3: Componente1.VIN, IC1.IN, VCC1.+, C2.0

notes:
  Servo MG-996R (180º)
  Voltaje: 4,8V - 6V
  600 - 1550mA
  Periodo PWM 20ms
  Torque: 9Kg
  Velocidad: 0,17s/60º
