# Fritzing sketch EyS_Analog (saved by Fritzing 0.9.2b)
breadboards: 1

parts:
  R1 = Resistor [tolerance=±5% resistance=220 package=THT]
  R1_2 = Rotary Potentiometer (Small) [maximum_resistance=10kΩ package=THT]
  LED1 = RGB LED (com. cathode, rgb) [package="5 mm [THT]"]
  Parte1 = Arduino Uno (Rev3)
  R3 = Rotary Potentiometer (Small) [maximum_resistance=10kΩ package=THT]
  R2 = Rotary Potentiometer (Small) [maximum_resistance=10kΩ package=THT]
  R4 = Resistor [tolerance=±5% resistance=100 package=THT]
  R5 = Resistor [tolerance=±5% resistance=100 package=THT]
  S1 = Pushbutton [package="[THT]"]
  R6 = Resistor [tolerance=±5% resistance=10k package=THT]

nets:
  N1: R1.Pin_0, LED1.red_anode
  N2: R1.Pin_1, Parte1.D11_PWM/MOSI
  N3: R1_2.leg1, Parte1.5V, R3.leg1, R2.leg1, S1.Pin_3, S1.Pin_4
  N4: R1_2.wiper, Parte1.A2
  N5: R1_2.leg2, LED1.common_cathode, Parte1.GND, R3.leg2, R2.leg2, R6.Pin_1
  N6: LED1.green_anode, R5.Pin_1
  N7: LED1.blue_anode, R4.Pin_1
  N8: Parte1.A0, R3.wiper
  N9: Parte1.A1, R2.wiper
  N10: Parte1.D9_PWM, R4.Pin_0
  N11: Parte1.D10_PWM/SS, R5.Pin_0
  N12: Parte1.D2, S1.Pin_1, S1.Pin_2, R6.Pin_0

// code stored in the sketch: E4_EyS_Analog.ino
/*  ----------------------------------------------------------------
Fco. Javier Rodriguez Navarro   www.pinguytaz.net

  
Probamos las entradas analogicas con potenciometros y la salida con
un led RGB
RGB conectado a PWM (11,10,9)
Ptocenciometros RGB (A2,A1,A0)


DATOS ALMACENAMIENTO:  32.256 bytes. (Programa) 2.048 (Variables)
      Programa 5.454  bytes (16%)
      V. Globales 276 bytes (13%)
--------------------------------------------------------------------  
*/

const int Rojo = 11; // pin 6 PWM para el rojo
const int Verde = 10; // pin 5 PWM del verde
const int Azul = 9; // pin 3 PWM del azul
const int PRojo = A2;
const int PVerde = A1;
const int PAzul = A0;
int pulsador = 2; // pin 2 asignado al pulsado


void setup() 
{
  // Definimos Pines
  pinMode(Rojo, OUTPUT); 
  pinMode(Verde, OUTPUT);
  pinMode(Azul, OUTPUT);
  pinMode(pulsador, INPUT); // declara pulsador como entrada

  // Apagamos el LED
  analogWrite(Rojo,0);
  analogWrite(Verde,0);
  analogWrite(Azul,0);

  Serial.begin(9600);    // abre el Puerto serie y lanza los primeros envios
  Serial.println("------ INICIO E/S Analogica -----"); 
}

void loop() 
{
  int rojo, verde, azul;
  int a_rojo, a_verde, a_azul;

  if (digitalRead(pulsador) == HIGH)
  {
     rojo = analogRead(PRojo);
     verde = analogRead(PVerde);
     azul = analogRead(PAzul);

     // Escalamos con la funcion map a valores entre 0 y 255.
     a_rojo = map(rojo,0,1023,0,255);
     a_verde = map(verde,0,1023,0,255);
     a_azul = map(azul,0,1023,0,255);

     // Informamos de los cambios para trazar por el serie
     Serial.println("ROJO: "+String(rojo)+" A "+String(a_rojo));
     Serial.println("VERDE: "+String(verde)+" A "+String(a_verde));
     Serial.println("AZUL: "+String(azul)+" A "+String(a_azul));


     // Iluminamos el LED con los valores obtenidos
     analogWrite(Rojo,a_rojo);
     analogWrite(Verde,a_verde);
     analogWrite(Azul,a_azul);

     delay(500); // Dejamos tiempo para soltar el boton
  }
  
}
