# Fritzing sketch MotorContinua (saved by Fritzing 0.9.3b)
breadboards: 1

parts:
  M1 = DC Motor
  R1 = Rotary Potentiometer (Small) [maximum_resistance=10kΩ package=THT]
  VCC1 = Battery block 9V
  R2 = Resistor [tolerance=±5% resistance=10k package=THT]
  Componente2 = Arduino Uno (Rev3)
  Q2 = Basic FET N-Channel [package="TO220 [THT]"]
  D1 = Rectifier Diode [part_number=1N4001 package="Melf DO-213 AB [SMD]"]

nets:
  N1: M1.pin_1, Q2.drain, D1.anode
  N2: M1.pin_2, VCC1.+, D1.cathode
  N3: R1.leg1, VCC1.-, R2.Pin_0, Componente2.GND, Q2.source
  N4: R1.wiper, Componente2.A0
  N5: R1.leg2, Componente2.5V
  N6: R2.Pin_1, Componente2.D3_PWM, Q2.gate

notes:
  10K
  GDS
