# Fritzing sketch Sonido (saved by Fritzing 0.9.2b)
breadboards: 1

parts:
  R1 = Resistor [tolerance=±5% resistance=470 package=THT]
  SPKR1 = Loudspeaker
  Parte1 = Arduino Uno (Rev3)

nets:
  N1: R1.Pin_0, Parte1.D7
  N2: R1.Pin_1, SPKR1.pin1
  N3: SPKR1.pin2, Parte1.GND
