# Fritzing sketch Analogico (saved by Fritzing 1.0.2b)
breadboards: 1

parts:
  R1 = Rotary Potentiometer (Small) [maximum_resistance=10kΩ knob_status=50% power=0.5W package=THT]
  Componente2 = Arduino Uno (Rev3)

nets:
  N1: R1.leg1, Componente2.GND
  N2: R1.wiper, Componente2.A0
  N3: R1.leg2, Componente2.5V
