# Fritzing sketch motor (saved by Fritzing 1.0.2b)
breadboards: 1

parts:
  Componente1 = Arduino Uno (Rev3)
  S1 = Pushbutton [package="[THT]"]
  VCC1 = Battery block 9V
  M1 = DC Motor [voltage_(max)=6V voltage_(min)=3V]
  R1 = Resistor [tolerance=±5% power=0.25W resistance=10k package=THT]
  D1 = Rectifier Diode [part_number=1N4001 package="300 mil [THT]"]
  Q1 = Basic FET N-Channel [part_number=IRF520 package="TO220 [THT]"]
  R2 = Resistor [tolerance=±5% power=0.25W resistance=10k package=THT]

nets:
  N1: Componente1.D12/MISO, Q1.gate, R2.Pin_0
  N2: Componente1.D2, S1.Pin_1, S1.Pin_2, R1.Pin_1
  N3: Componente1.5V, S1.Pin_3, S1.Pin_4
  N4: Componente1.GND, VCC1.-, R1.Pin_0, Q1.source, R2.Pin_1
  N5: VCC1.+, M1.pin_1, D1.cathode
  N6: M1.pin_2, D1.anode, Q1.drain

notes:
  GDS
