# Fritzing sketch EsqEjWS2812 (saved by Fritzing 0.9.10b)
breadboards: 1

parts:
  Componente1 = Arduino Uno (Rev3)
  R1 = Resistor [tolerance=±5% resistance=470 package="0603 [SMD]"]
  C1 = Electrolytic Capacitor [capacitance=100μF voltage=35V package="0807 [SMD, electrolytic]"]
  U2 = WS2812 RGB LED strip
  VCC1 = Battery block 9V
  IC1 = Voltage Regulator [package=to-220-alt]

nets:
  N1: Componente1.D12/MISO, U2.DIN
  GND: Componente1.GND, C1.-, U2.GND, VCC1.-, IC1.IN
  N2: Componente1.VIN, R1.Pin_0, C1.+, IC1.OUT
  N3: R1.Pin_1, U2.VCC
  N4: VCC1.+, IC1.GND

custom parts:
  WS2812 RGB LED strip: WS2812 strip
