# Fritzing sketch E_Analogicas (saved by Fritzing 0.9.3b)
breadboards: 1

parts:
  Componente1 = Arduino Uno (Rev3)
  T1 = TMP36 Temperature Sensor [package="TO92 [THT]"]
  R1 = Trimmer Potentiometer [maximum_resistance=10kΩ package=THT]

nets:
  N1: Componente1.A0, T1.Vout
  N2: Componente1.A1, R1.wiper
  GND: Componente1.GND, T1.GND, R1.leg1
  N3: Componente1.3V3, R1.leg2
  N4: Componente1.5V, T1.+Vs
