# Fritzing sketch TestResistencia (saved by Fritzing 0.9.3b)
breadboards: 1

parts:
  Componente1 = Arduino Nano (Rev3.0)
  R1 = Resistor [tolerance=±5% resistance=10k package=THT]
  S1 = Pushbutton [package="[THT]"]
  R5 = Resistor [tolerance=±5% resistance=2.2k package=THT]
  R6 = Resistor [tolerance=±5% resistance=22k package=THT]
  R7 = Resistor [tolerance=±5% resistance=220k package=THT]
  R8 = Resistor [tolerance=±5% resistance=1M package=THT]

nets:
  N1: Componente1.GND, R1.Pin_1, S1.Pin_3, S1.Pin_4
  R?1: Componente1.D2
  N2: Componente1.D3, R8.Pin_0
  N3: Componente1.D4, R7.Pin_0
  N4: Componente1.D5, R6.Pin_0
  N5: Componente1.D6, R5.Pin_0
  N6: Componente1.D12/MISO, R1.Pin_0
  N7: Componente1.5V, S1.Pin_1, S1.Pin_2
  SCL LCD: Componente1.A5
  SDA LCD: Componente1.A4
  R?2: Componente1.A0, R5.Pin_1, R6.Pin_1, R7.Pin_1, R8.Pin_1
