# Fritzing sketch Ejemplo6 (saved by Fritzing 0.9.3b)
breadboards: 1

parts:
  Componente1 = Arduino Nano (Rev3.0)
  R1 = Resistor [tolerance=±5% resistance=220 package=THT]
  Rojo = LED - 5mm [color="Green (555nm)" package="5 mm [THT]"]
  R4 = Resistor [tolerance=±5% resistance=220 package=THT]
  Naranja = LED - 5mm [color="Green (555nm)" package="5 mm [THT]"]
  Verde = LED - 5mm [color="Green (555nm)" package="5 mm [THT]"]
  R5 = Resistor [tolerance=±5% resistance=220 package=THT]
  R6 = Resistor [tolerance=±5% resistance=10k package=THT]
  S1 = Pushbutton [package="[THT]"]

nets:
  N1: Componente1.GND, Rojo.cathode, Naranja.cathode, Verde.cathode, R6.Pin_0
  N2: Componente1.D2, R1.Pin_0
  N3: Componente1.D4, R4.Pin_0
  N4: Componente1.D7, R5.Pin_0
  N5: Componente1.D12/MISO, R6.Pin_1, S1.Pin_1, S1.Pin_2
  N6: Componente1.5V, S1.Pin_3, S1.Pin_4
  N7: R1.Pin_1, Rojo.anode
  N8: R4.Pin_1, Naranja.anode
  N9: Verde.anode, R5.Pin_1
